# Fritzing sketch StairsV1 (saved by Fritzing 0.9.2b)
circuit board: 7cm x 5.24687cm
breadboards: 1

parts:
  Q1 = Basic FET P-Channel [package="TO220 [THT]"]
  Q2 = Basic FET P-Channel [package="TO220 [THT]"]
  R1 = Resistor [tolerance=±5% resistance=220 package=THT]
  Súčiastka1 = Arduino Nano (Rev3.0)
  Vcc = screw terminal, 2 pins
  PIRs = screw terminal, 5 pins
  R2 = Resistor [tolerance=±5% resistance=220 package=THT]
  LED_out = screw terminal, 4 pins
  R3 = Photocell (LDR) [package=THT]
  LDR_in = screw terminal, 2 pins

nets:
  N1: Q1.gate, Súčiastka1.D6
  N2: Q1.drain, LED_out.pin3
  N3: Q1.source, Q2.source, R1.Pin_0, Súčiastka1.GND, Vcc.pin2, PIRs.pin2, R2.Pin_0
  N4: Q2.gate, Súčiastka1.D9
  N5: Q2.drain, LED_out.pin4
  N6: R1.Pin_1, Súčiastka1.A1, R3.pin_1
  N7: Súčiastka1.D3, PIRs.pin3
  N8: Súčiastka1.D4, PIRs.pin4
  N9: Súčiastka1.D5, PIRs.pin5
  N10: Súčiastka1.VIN, Vcc.pin1, PIRs.pin1, LED_out.pin1, LED_out.pin2
  N11: Súčiastka1.5V, R3.pin_0, LDR_in.pin1
  N12: Súčiastka1.A2, R2.Pin_1, LDR_in.pin2
